// Digital circuit template registradorPC.dig as structural Verilog
module template_registradorPC (
  input  [31:0] A,
  input  Clk,
  input  Rst,
  output [31:0] Y
);

  RegistradorPC #(.applicationType("IVERILOG")) u_RegistradorPC (.A(A), .Clk(Clk), .Rst(Rst), .Y(Y));
endmodule

/* Test case ULA:
Clk A Rst Y
 loop(i,10)
   let a = random(1<<16);
   c (a) 0 0
   c (a) 1 (a)
  end loop
*/

/* Code of RegistradorPC:
module RegistradorPC(input A, Clk, Rst, output Y);
     
endmodule
*/
